# Fritzing sketch HAR Circuit (saved by Fritzing 0.9.3b)

parts:
  U1 = NodeMCU V1.0
  Part1 = InvenSense MPU6050
  U2 = SWITCH-SPST-2 [package=r_sw_th]
  J1 = Power Jack [package=power_jack_slot]
  LED1 = smd LED [color="Red (633nm)" package="0805 [SMD]"]
  IC1 = Voltage Regulator [package=to-92]
  BAT2 = Battery Holders [package=battery-aa]
  R1 = Resistor [tolerance=±5% resistance=220 package="1206 [SMD]"]
  TP1 = TP4056 [chip_label=TP4056 package="DIP (Dual Inline) [THT]"]

nets:
  N1: U1.D1, Part1.SCL
  N2: U1.D2, Part1.SDA
  3V3: U1.3V3, Part1.VCC
  GND: U1.GND, Part1.GND, LED1.cathode, IC1.GND, TP1.pin6
  N3: U1.Vin, IC1.OUT
  N4: U2.O, IC1.IN
  N5: U2.P, R1.Pin_0, TP1.pin3
  N6: J1.GND, TP1.pin2
  N7: J1.PWR, TP1.pin1
  N8: BAT2.-, TP1.pin5
  N9: BAT2.+, TP1.pin4

custom parts:
  NodeMCU V1.0: ESP8266 based NodeMCU
  TP4056: A DIP stand-in part for whatever IC you want. With 6 pins on a 300mil dual inline package (DIP) footprint.
